// Logisim project ep2.circ as structural Verilog: 13 circuits, main circuit ALU
module ALU (
  input  [15:0] in_1,
  input  [15:0] in_2,
  input  [2:0] s,
  input  Set_mode,
  input  Clear,
  output Overflow,
  output Div0,
  output [15:0] out_8
);

  wire adder_8_bits_1_carry_out, comparator_2_eq, E0, Overflow_Add, Overflow_Mult, Overflow_Sub;
  wire [15:0] \Adição , \Divisão , \Multiplicação , multiplier_1_cout, Resto, Result, \Subtração ;

  Adder_8_bits adder_8_bits_1 (
    .Carry_Out(adder_8_bits_1_carry_out), .Carry_in(1'b0), .in_2(in_1[7:0]), .in_3(in_2[7:0]),
    .out_4(\Adição [7:0]));  // open: Overflow
  Adder_8_bits adder_8_bits_2 (
    .Overflow(Overflow_Add), .Carry_in(adder_8_bits_1_carry_out), .in_2(in_1[15:8]), .in_3(in_2[15:8]),
    .out_4(\Adição [15:8]));  // open: Carry_Out
  Subtractor #(.width(16)) subtractor_1 (.a(in_1), .b(in_2), .out(\Subtração ), .bout(Overflow_Sub));  // open: bin
  Comparator #(.width(16)) comparator_1 (.a(in_2), .b({16{1'b0}}), .eq(E0));  // open: gt, lt
  Multiplier #(.width(16)) multiplier_1 (
    .a(in_1), .b(in_2), .out(\Multiplicação ), .cout(multiplier_1_cout));  // open: cin
  or or_1 (Overflow_Mult, multiplier_1_cout[15], multiplier_1_cout[14], multiplier_1_cout[13], multiplier_1_cout[12], multiplier_1_cout[11], multiplier_1_cout[10], multiplier_1_cout[9], multiplier_1_cout[8], multiplier_1_cout[7], multiplier_1_cout[6], multiplier_1_cout[5], multiplier_1_cout[4], multiplier_1_cout[3], multiplier_1_cout[2], multiplier_1_cout[1], multiplier_1_cout[0]);
  Divider #(.width(16)) divider_1 (.a(in_1), .b(in_2), .out(\Divisão ), .rem(Resto));  // open: upper
  Multiplexer #(.select(3)) multiplexer_1 (
    .in0(Overflow_Add), .in1(Overflow_Sub), .in2(Overflow_Mult), .in3(1'b0), .in4(1'b0), .in5(1'b0),
    .in6(1'b0), .in7(1'b0), .out(Overflow), .sel(s), .en(1'b1));
  Multiplexer #(.select(3), .width(16), .enable("false")) multiplexer_2 (
    .in0(\Adição ), .in1(\Subtração ), .in2(\Multiplicação ), .in3(\Divisão ), .in4(Resto), .in5({16{1'b0}}),
    .in6({16{1'b0}}), .in7({16{1'b0}}), .out(Result), .sel(s));
  and and_1 (Div0, E0, comparator_2_eq);
  Comparator #(.width(3)) comparator_2 (.a(s), .b(3'b011), .eq(comparator_2_eq));  // open: gt, lt
  Register #(.width(16), .trigger("high")) register_1 (.D(Result), .en(Set_mode), .Q(out_8), .clk(1'b1), .clr(Clear));

  // Other names for the same wires on the sheet: A[15:0] = in_1; A1[7:0] = in_1[7:0]; A2[7:0] = in_1[15:8];
  //   B[15:0] = in_2; B1[7:0] = in_2[7:0]; B2[7:0] = in_2[15:8]
endmodule

module half_Adder (
  input  a,
  input  b,
  output Carry,
  output Out
);

  and and_1 (Carry, a, b);
  xor xor_1 (Out, a, b);
endmodule

module Full_Adder (
  input  Carry_in,
  input  a_in,
  input  b_in,
  output Result,
  output Carry
);

  wire half_adder_1_carry, half_adder_1_out, half_adder_2_carry;

  half_Adder half_adder_1 (.a(a_in), .b(b_in), .Carry(half_adder_1_carry), .Out(half_adder_1_out));
  half_Adder half_adder_2 (.a(Carry_in), .b(half_adder_1_out), .Carry(half_adder_2_carry), .Out(Result));
  or or_1 (Carry, half_adder_2_carry, half_adder_1_carry);
endmodule

module Adder_8_bits (
  input  Carry_in,
  input  [7:0] in_2,
  input  [7:0] in_3,
  output [7:0] out_4,
  output Overflow,
  output Carry_Out
);

  wire and_1_out, and_2_out, and_3_out, and_4_out, full_adder_1_carry, full_adder_2_carry,
       full_adder_3_carry, full_adder_4_carry, full_adder_5_carry, full_adder_6_carry, full_adder_7_carry,
       not_1_out, not_2_out, not_3_out;

  Full_Adder full_adder_1 (
    .Carry_in(Carry_in), .a_in(in_2[0]), .b_in(in_3[0]), .Result(out_4[0]), .Carry(full_adder_1_carry));
  Full_Adder full_adder_2 (
    .Carry_in(full_adder_1_carry), .a_in(in_2[1]), .b_in(in_3[1]), .Result(out_4[1]),
    .Carry(full_adder_2_carry));
  Full_Adder full_adder_3 (
    .Carry_in(full_adder_2_carry), .a_in(in_2[2]), .b_in(in_3[2]), .Result(out_4[2]),
    .Carry(full_adder_3_carry));
  Full_Adder full_adder_4 (
    .Carry_in(full_adder_3_carry), .a_in(in_2[3]), .b_in(in_3[3]), .Result(out_4[3]),
    .Carry(full_adder_4_carry));
  Full_Adder full_adder_5 (
    .Carry_in(full_adder_4_carry), .a_in(in_2[4]), .b_in(in_3[4]), .Result(out_4[4]),
    .Carry(full_adder_5_carry));
  Full_Adder full_adder_6 (
    .Carry_in(full_adder_5_carry), .a_in(in_2[5]), .b_in(in_3[5]), .Result(out_4[5]),
    .Carry(full_adder_6_carry));
  Full_Adder full_adder_7 (
    .Carry_in(full_adder_6_carry), .a_in(in_2[6]), .b_in(in_3[6]), .Result(out_4[6]),
    .Carry(full_adder_7_carry));
  Full_Adder full_adder_8 (
    .Carry_in(full_adder_7_carry), .a_in(in_2[7]), .b_in(in_3[7]), .Result(out_4[7]), .Carry(Carry_Out));
  not not_1 (not_1_out, in_2[7]);
  not not_2 (not_2_out, in_3[7]);
  and and_1 (and_1_out, in_2[7], in_3[7]);
  not not_3 (not_3_out, out_4[7]);
  and and_2 (and_2_out, not_1_out, not_2_out);
  and and_3 (and_3_out, and_2_out, out_4[7]);
  and and_4 (and_4_out, and_1_out, not_3_out);
  or or_1 (Overflow, and_3_out, and_4_out);

  // Other names for the same wires on the sheet: a7 = in_2[7]; b7 = in_3[7]; r7 = out_4[7]

  // Notes on the sheet:
  //   a0
  //   a1
  //   a2
  //   a5
  //   a6
  //   a7
  //   b0
  //   b1
  //   b5
  //   b6
  //   b7
  //   a3
  //   a4
  //   b2
  //   b3
  //   b4
  //   r0
  //   r1
  //   r2
  //   r3
  //   r4
  //   r5
  //   r6
  //   r7
endmodule

module Two_s_complement (
  input  in_1,
  input  in_2,
  input  in_3,
  input  in_4,
  input  in_5,
  input  in_6,
  input  in_7,
  input  in_8,
  output out_9,
  output out_10,
  output out_11,
  output out_12,
  output out_13,
  output out_14,
  output out_15,
  output out_16,
  output out_17
);

  wire not_1_out, not_2_out, not_3_out, not_4_out, not_5_out, not_6_out, not_7_out, not_8_out;

  not not_1 (not_1_out, in_1);
  not not_2 (not_2_out, in_2);
  not not_3 (not_3_out, in_3);
  not not_4 (not_4_out, in_4);
  not not_5 (not_5_out, in_5);
  not not_6 (not_6_out, in_6);
  not not_7 (not_7_out, in_7);
  not not_8 (not_8_out, in_8);
  // Adder_8_bits adder_8_bits_1: pin names not known; wires that end beside it: not_1_out, not_2_out, not_3_out, not_4_out, not_5_out, not_6_out, not_7_out, not_8_out, 1'b1, 1'b0, out_9, out_10, out_11, out_12, out_13, out_14, out_15, out_16, out_17
endmodule

module Subtraction (
  input  [15:0] in_1,
  input  [15:0] in_2,
  output [15:0] out_3,
  output Overflow
);

  wire adder_8_bits_1_carry_out;
  wire [15:0] negator_1_out;

  Negator #(.width(16)) negator_1 (.in(in_2), .out(negator_1_out));
  Adder_8_bits adder_8_bits_1 (
    .Carry_Out(adder_8_bits_1_carry_out), .Carry_in(1'b0), .in_2(in_1[7:0]), .in_3(negator_1_out[7:0]),
    .out_4(out_3[7:0]));  // open: Overflow
  Adder_8_bits adder_8_bits_2 (
    .Overflow(Overflow), .Carry_in(adder_8_bits_1_carry_out), .in_2(in_1[15:8]), .in_3(negator_1_out[15:8]),
    .out_4(out_3[15:8]));  // open: Carry_Out
endmodule

module Quarter_Multiplier (
  input  [7:0] in_1,
  input  in_2,
  output [7:0] out_3,
  output [7:0] out_4
);

  Shifter shifter_1 (.in(in_1), .\dist (3'b001), .out(out_3));
  and and_1 (out_4[0], in_2, in_1[0]);
  and and_2 (out_4[1], in_2, in_1[1]);
  and and_3 (out_4[2], in_2, in_1[2]);
  and and_4 (out_4[3], in_2, in_1[3]);
  and and_5 (out_4[4], in_2, in_1[4]);
  and and_6 (out_4[5], in_2, in_1[5]);
  and and_7 (out_4[6], in_2, in_1[6]);
  and and_8 (out_4[7], in_2, in_1[7]);
endmodule

module Full_Multiplier_8 (
  input  a0,
  input  a1,
  input  a2,
  input  a3,
  input  a4,
  input  a5,
  input  a6,
  input  a7,
  input  b0,
  input  b1,
  input  b2,
  input  b3,
  input  b4,
  input  b5,
  input  b6,
  input  b7,
  output out_17,
  output out_18,
  output out_19,
  output out_20,
  output out_21,
  output out_22,
  output out_23,
  output out_24,
  output out_25,
  output out_26
);

  wire and_1_out, and_2_out, and_3_out, and_4_out, and_5_out, and_6_out, or_2_out, or_3_out, or_4_out,
       or_5_out, or_6_out, quarter_multiplier_8_p2, undriven, undriven_2, undriven_3, undriven_4, undriven_5,
       undriven_6, undriven_7;
  wire [5:3] m1, m2, m3, m4, m5, m6;
  wire [7:0] quarter_multiplier_1_out_3, quarter_multiplier_2_out_3, quarter_multiplier_3_out_3,
       quarter_multiplier_4_out_3, quarter_multiplier_5_out_3, quarter_multiplier_6_out_3,
       quarter_multiplier_7_out_3, r0, r1, r2, r3, r4, r5, r6, r7;

  Quarter_Multiplier quarter_multiplier_1 (
    .in_1({b7, b6, b5, b4, b3, b2, b1, b0}), .in_2(a0), .out_3(quarter_multiplier_1_out_3), .out_4(r0));
  Quarter_Multiplier quarter_multiplier_2 (
    .in_1(quarter_multiplier_1_out_3), .in_2(a1), .out_3(quarter_multiplier_2_out_3), .out_4(r1));
  Quarter_Multiplier quarter_multiplier_3 (
    .in_1(quarter_multiplier_2_out_3), .in_2(a2), .out_3(quarter_multiplier_3_out_3), .out_4(r2));
  Quarter_Multiplier quarter_multiplier_4 (
    .in_1(quarter_multiplier_3_out_3), .in_2(a3), .out_3(quarter_multiplier_4_out_3), .out_4(r3));
  Quarter_Multiplier quarter_multiplier_5 (
    .in_1(quarter_multiplier_4_out_3), .in_2(a4), .out_3(quarter_multiplier_5_out_3), .out_4(r4));
  Quarter_Multiplier quarter_multiplier_6 (
    .in_1(quarter_multiplier_5_out_3), .in_2(a5), .out_3(quarter_multiplier_6_out_3), .out_4(r5));
  Quarter_Multiplier quarter_multiplier_7 (
    .in_1(quarter_multiplier_6_out_3), .in_2(a6), .out_3(quarter_multiplier_7_out_3), .out_4(r6));
  // Adder_8_bits adder_8_bits_1: pin names not known; wires that end beside it: r0[5], r1[1], m1[3]
  // Adder_8_bits adder_8_bits_2: pin names not known; wires that end beside it: m5[5], r6[1], m6[3]
  // Quarter_Multiplier quarter_multiplier_8: pin names not known; wires that end beside it: quarter_multiplier_7_out_3, quarter_multiplier_8_p2, a7, r7
  or or_1 (out_26, quarter_multiplier_8_p2, undriven_7, undriven_6, undriven_5, undriven_4, undriven_3, undriven_2, undriven);
  // Adder_8_bits adder_8_bits_3: pin names not known; wires that end beside it: m1[5], r2[1], m2[3]
  // Adder_8_bits adder_8_bits_4: pin names not known; wires that end beside it: m6[5], r7[1], out_20
  // Adder_8_bits adder_8_bits_5: pin names not known; wires that end beside it: m2[5], r3[1], m3[3]
  // Adder_8_bits adder_8_bits_6: pin names not known; wires that end beside it: m3[5], r4[1], m4[3]
  // Adder_8_bits adder_8_bits_7: pin names not known; wires that end beside it: m4[5], r5[1], m5[3]
  or or_2 (or_2_out, a2, a3, a4, a5, a5, a6);
  or or_3 (or_3_out, a1, a2, a3, a4, a5, a6);
  or or_4 (or_4_out, a3, a4, a5, a6);
  or or_5 (or_5_out, a4, a5, a6);
  or or_6 (or_6_out, a5, a6);
  and and_1 (and_1_out, or_2_out, b5);
  and and_2 (and_2_out, b1, a6);
  and and_3 (and_3_out, b6, or_3_out);
  and and_4 (and_4_out, b4, or_4_out);
  and and_5 (and_5_out, b3, or_5_out);
  and and_6 (and_6_out, b2, or_6_out);
  or or_7 (out_24, and_1_out, and_2_out, and_3_out, and_4_out, and_5_out, and_6_out);

  // Other names for the same wires on the sheet: m7[7:0] = {out_25, out_23, out_22, out_21, out_20, out_19, out_18, out_17}
endmodule

module Modulo (
  input  a0,
  input  a1,
  input  a2,
  input  a3,
  input  a4,
  input  a5,
  input  a6,
  input  a7,
  input  Flag,
  output out_10,
  output out_11,
  output out_12,
  output out_13,
  output out_14,
  output out_15,
  output out_16,
  output out_17
);

  wire xor0, xor1, xor2, xor3, xor4, xor5, xor6, xor7;

  xor xor_1 (xor0, a0, Flag);
  xor xor_2 (xor1, a1, Flag);
  xor xor_3 (xor2, a2, Flag);
  xor xor_4 (xor3, a3, Flag);
  // Adder_8_bits adder_8_bits_1: pin names not known; wires that end beside it: xor0, xor1, xor2, xor3, xor4, xor5, xor6, xor7, Flag, 1'b0, out_10, out_11, out_12, out_13, out_14, out_15, out_16, out_17
  xor xor_5 (xor4, a4, Flag);
  xor xor_6 (xor5, a5, Flag);
  xor xor_7 (xor6, a6, Flag);
  xor xor_8 (xor7, a7, Flag);
endmodule

module Final_Multiplier (
  input  a0,
  input  a1,
  input  a2,
  input  a3,
  input  a4,
  input  a5,
  input  a6,
  input  a7,
  input  b0,
  input  b1,
  input  b2,
  input  b3,
  input  b4,
  input  b5,
  input  b6,
  input  b7,
  output r0,
  output r1,
  output r2,
  output r3,
  output r4,
  output r5,
  output r6,
  output r7,
  output out_25
);

  wire Flag;
  wire [7:0] Mod1, Mod2, R1_t;

  Modulo Modulo (
    .a0(a0), .a1(a1), .a2(a2), .a3(a3), .a4(a4), .a5(a5), .a6(a6), .a7(a7), .Flag(a7), .out_10(Mod1[0]),
    .out_11(Mod1[1]), .out_12(Mod1[2]), .out_13(Mod1[3]), .out_14(Mod1[4]), .out_15(Mod1[5]),
    .out_16(Mod1[6]), .out_17(Mod1[7]));
  Modulo Modulo_2 (
    .a0(b0), .a1(b1), .a2(b2), .a3(b3), .a4(b4), .a5(b5), .a6(b6), .a7(b7), .Flag(b7), .out_10(Mod2[0]),
    .out_11(Mod2[1]), .out_12(Mod2[2]), .out_13(Mod2[3]), .out_14(Mod2[4]), .out_15(Mod2[5]),
    .out_16(Mod2[6]), .out_17(Mod2[7]));
  Full_Multiplier_8 full_multiplier_8_1 (
    .a0(Mod1[0]), .b0(Mod2[0]), .a1(Mod1[1]), .b1(Mod2[1]), .a2(Mod1[2]), .b2(Mod2[2]), .a3(Mod1[3]),
    .b3(Mod2[3]), .a4(Mod1[4]), .b4(Mod2[4]), .a5(Mod1[5]), .b5(Mod2[5]), .a6(Mod1[6]), .b6(Mod2[6]),
    .a7(Mod1[7]), .b7(Mod2[7]), .out_17(R1_t[0]), .out_18(R1_t[1]), .out_19(R1_t[2]), .out_20(R1_t[3]),
    .out_21(R1_t[4]), .out_22(R1_t[5]), .out_23(R1_t[6]), .out_25(R1_t[7]), .out_24(out_25));  // open: out_26
  xor xor_1 (Flag, a7, b7);
  Modulo modulo_3 (
    .a0(R1_t[0]), .a1(R1_t[1]), .a2(R1_t[2]), .a3(R1_t[3]), .a4(R1_t[4]), .a5(R1_t[5]), .a6(R1_t[6]),
    .a7(R1_t[7]), .Flag(Flag), .out_10(r0), .out_11(r1), .out_12(r2), .out_13(r3), .out_14(r4), .out_15(r5),
    .out_16(r6), .out_17(r7));

  // Other names for the same wires on the sheet: Overflow = out_25; Result[7:0] = {r7, r6, r5, r4, r3, r2, r1, r0}
endmodule

module \Divisão  (
  input  a0,
  input  a1,
  input  a2,
  input  a3,
  input  a4,
  input  a5,
  input  a6,
  input  a7,
  input  b0,
  input  b1,
  input  b2,
  input  b3,
  input  b4,
  input  b5,
  input  b6,
  input  b7,
  output r0,
  output r1,
  output r2,
  output r3,
  output r4,
  output r5,
  output r6,
  output r7
);

  wire and_1_out, clock_1_out, not_1_out, not_2_out, or_1_out, or_2_out, undriven;
  wire [7:0] counter_1_q, multiplexer_1_out, register_1_q, subtraction_2_p16;

  or or_1 (or_1_out, counter_1_q[0], counter_1_q[1], counter_1_q[2], counter_1_q[3], counter_1_q[4], counter_1_q[5], counter_1_q[6], counter_1_q[7]);
  Multiplexer #(.width(8)) multiplexer_1 (
    .in0({a7, a6, a5, a4, a3, a2, a1, a0}), .in1(subtraction_2_p16), .out(multiplexer_1_out), .sel(or_1_out),
    .en(not_1_out));
  not not_1 (not_1_out, register_1_q[7]);
  // Subtraction subtraction_1: pin names not known; wires that end beside it: counter_1_q[1], counter_1_q[2], counter_1_q[3], counter_1_q[4], counter_1_q[5], counter_1_q[6], counter_1_q[7], 1'b0, 1'b1, 1'b0, 1'b0, 1'b0, 1'b0, 1'b0, 1'b0, r0, r1, r2, r3, r4, r5, r6, r7
  Counter counter_1 (.Q(counter_1_q), .clk(and_1_out));  // open: load, D, count, carry, clr
  Register register_1 (.D(multiplexer_1_out), .en(undriven), .Q(register_1_q), .clk(and_1_out));  // open: clr
  and and_1 (and_1_out, not_2_out, or_2_out, clock_1_out);
  not not_2 (not_2_out, register_1_q[7]);
  Clock clock_1 (.out(clock_1_out));
  or or_2 (or_2_out, b0, b1, b2, b3, b4, b5, b6, b7);
  // Subtraction subtraction_2: pin names not known; wires that end beside it: register_1_q[1], register_1_q[2], register_1_q[3], register_1_q[4], register_1_q[5], register_1_q[6], register_1_q[7], b0, b1, b2, b3, b4, b5, b6, b7, subtraction_2_p16[0], subtraction_2_p16[1], subtraction_2_p16[2], subtraction_2_p16[3], subtraction_2_p16[4], subtraction_2_p16[5], subtraction_2_p16[6], subtraction_2_p16[7]

  // Notes on the sheet:
  //   DIVIDENDO
  //   DIVISOR
endmodule

module Final_Divider (
  input  a0,
  input  a1,
  input  a2,
  input  a3,
  input  a4,
  input  a5,
  input  a6,
  input  a7,
  input  b0,
  input  b1,
  input  b2,
  input  b3,
  input  b4,
  input  b5,
  input  b6,
  input  b7,
  output out_17,
  output out_18,
  output out_19,
  output out_20,
  output out_21,
  output out_22,
  output out_23,
  output out_24
);

  wire Flag;
  wire [7:0] Mod1, Mod2, R1;

  Modulo Modulo (
    .a0(a0), .a1(a1), .a2(a2), .a3(a3), .a4(a4), .a5(a5), .a6(a6), .a7(a7), .Flag(a7), .out_10(Mod1[0]),
    .out_11(Mod1[1]), .out_12(Mod1[2]), .out_13(Mod1[3]), .out_14(Mod1[4]), .out_15(Mod1[5]),
    .out_16(Mod1[6]), .out_17(Mod1[7]));
  Modulo Modulo_2 (
    .a0(b0), .a1(b1), .a2(b2), .a3(b3), .a4(b4), .a5(b5), .a6(b6), .a7(b7), .Flag(b7), .out_10(Mod2[0]),
    .out_11(Mod2[1]), .out_12(Mod2[2]), .out_13(Mod2[3]), .out_14(Mod2[4]), .out_15(Mod2[5]),
    .out_16(Mod2[6]), .out_17(Mod2[7]));
  \Divisão  \divisão_1  (
    .a0(Mod1[0]), .a1(Mod1[1]), .a2(Mod1[2]), .a3(Mod1[3]), .a4(Mod1[4]), .a5(Mod1[5]), .a6(Mod1[6]),
    .a7(Mod1[7]), .b0(Mod2[0]), .b1(Mod2[1]), .b2(Mod2[2]), .b3(Mod2[3]), .b4(Mod2[4]), .b5(Mod2[5]),
    .b6(Mod2[6]), .b7(Mod2[7]), .r0(R1[0]), .r1(R1[1]), .r2(R1[2]), .r3(R1[3]), .r4(R1[4]), .r5(R1[5]),
    .r6(R1[6]), .r7(R1[7]));
  xor xor_1 (Flag, a7, b7);
  Modulo modulo_3 (
    .a0(R1[0]), .a1(R1[1]), .a2(R1[2]), .a3(R1[3]), .a4(R1[4]), .a5(R1[5]), .a6(R1[6]), .a7(R1[7]),
    .Flag(Flag), .out_10(out_17), .out_11(out_18), .out_12(out_19), .out_13(out_20), .out_14(out_21),
    .out_15(out_22), .out_16(out_23), .out_17(out_24));

  // Other names for the same wires on the sheet: Result[7:0] = {out_24, out_23, out_22, out_21, out_20, out_19, out_18, out_17}
endmodule

module Resto (
  input  a0,
  input  a1,
  input  a2,
  input  a3,
  input  a4,
  input  a5,
  input  a6,
  input  a7,
  input  b0,
  input  b1,
  input  b2,
  input  b3,
  input  b4,
  input  b5,
  input  b6,
  input  b7,
  output out_17,
  output out_18,
  output out_19,
  output out_20,
  output out_21,
  output out_22,
  output out_23,
  output out_24
);

  wire final_divider_1_out_17, final_divider_1_out_18, final_divider_1_out_19, final_divider_1_out_20,
       final_divider_1_out_21, final_divider_1_out_22, final_divider_1_out_23, final_divider_1_out_24,
       final_multiplier_1_r0, final_multiplier_1_r1, final_multiplier_1_r2, final_multiplier_1_r3,
       final_multiplier_1_r4, final_multiplier_1_r5, final_multiplier_1_r6, final_multiplier_1_r7, Flag;
  wire [7:0] Result;

  Final_Divider final_divider_1 (
    .a0(a0), .a1(a1), .a2(a2), .a3(a3), .a4(a4), .a5(a5), .a6(a6), .a7(a7), .b0(b0), .b1(b1), .b2(b2),
    .b3(b3), .b4(b4), .b5(b5), .b6(b6), .b7(b7), .out_17(final_divider_1_out_17),
    .out_18(final_divider_1_out_18), .out_19(final_divider_1_out_19), .out_20(final_divider_1_out_20),
    .out_21(final_divider_1_out_21), .out_22(final_divider_1_out_22), .out_23(final_divider_1_out_23),
    .out_24(final_divider_1_out_24));
  Final_Multiplier final_multiplier_1 (
    .a0(final_divider_1_out_17), .a1(final_divider_1_out_18), .a2(final_divider_1_out_19),
    .a3(final_divider_1_out_20), .a4(final_divider_1_out_21), .a5(final_divider_1_out_22),
    .a6(final_divider_1_out_23), .a7(final_divider_1_out_24), .b0(b0), .b1(b1), .b2(b2), .b3(b3), .b4(b4),
    .b5(b5), .b6(b6), .b7(b7), .r0(final_multiplier_1_r0), .r1(final_multiplier_1_r1),
    .r2(final_multiplier_1_r2), .r3(final_multiplier_1_r3), .r4(final_multiplier_1_r4),
    .r5(final_multiplier_1_r5), .r6(final_multiplier_1_r6), .r7(final_multiplier_1_r7));  // open: out_25
  xor xor_1 (Flag, a7, b7);
  // Subtraction subtraction_1: pin names not known; wires that end beside it: a1, a2, a3, a4, a5, a6, a7, final_multiplier_1_r0, final_multiplier_1_r1, final_multiplier_1_r2, final_multiplier_1_r3, final_multiplier_1_r4, final_multiplier_1_r5, final_multiplier_1_r6, final_multiplier_1_r7, Result[5]
  Modulo modulo_1 (
    .a0(Result[0]), .a1(Result[1]), .a2(Result[2]), .a3(Result[3]), .a4(Result[4]), .a5(Result[5]),
    .a6(Result[6]), .a7(Result[7]), .Flag(Flag), .out_10(out_17), .out_11(out_18), .out_12(out_19),
    .out_13(out_20), .out_14(out_21), .out_15(out_22), .out_16(out_23), .out_17(out_24));
endmodule
