// Logisim project Projeto.circ as structural Verilog: 3 circuits, main circuit PC
module PC (
  input  in_1,
  input  in_2,
  input  [7:0] in_3,
  output [7:0] out_4
);

  wire and_1_out, and_2_out, and_3_out, and_4_out, and_5_out, and_6_out, and_7_out, and_8_out, and_9_out,
       and_10_out, and_11_out, and_12_out, and_13_out, and_14_out, and_15_out, and_16_out, and_17_out,
       and_18_out, and_19_out, and_20_out, and_21_out, and_22_out, and_23_out, and_24_out, and_25_out,
       and_26_out, and_27_out, and_31_out, and_32_out, and_33_out, and_34_out, and_35_out, and_36_out,
       and_37_out, and_38_out, and_39_out, not_1_out, not_2_out, not_3_out, not_4_out, not_5_out, not_6_out,
       not_7_out, not_8_out, not_9_out, not_10_out, not_11_out, not_12_out, not_13_out, not_14_out,
       not_15_out, not_16_out, pulso2, pulso4, pulso6, pulso8;

  not not_1 (not_1_out, out_4[0]);
  and and_1 (and_1_out, 1'b1, not_1_out);
  and and_2 (and_2_out, 1'b1, out_4[0]);
  and and_3 (and_3_out, in_3[0], in_2);
  not not_2 (not_2_out, in_3[0]);
  not not_3 (not_3_out, out_4[2]);
  and and_4 (and_4_out, pulso2, not_3_out);
  and and_5 (and_5_out, out_4[2], pulso2);
  and and_6 (and_6_out, in_3[2], in_2);
  not not_4 (not_4_out, in_3[2]);
  not not_5 (not_5_out, out_4[4]);
  and and_7 (and_7_out, pulso4, not_5_out);
  and and_8 (and_8_out, out_4[4], pulso4);
  and and_9 (and_9_out, in_3[4], in_2);
  not not_6 (not_6_out, in_3[4]);
  J_K_Flip_Flop j_k_ff_1 (
    .J(and_1_out), .clk(in_1), .K(and_2_out), .Q(out_4[0]), .preset(and_3_out), .reset(and_10_out));  // open: Qn, en
  and and_10 (and_10_out, not_2_out, in_2);
  J_K_Flip_Flop j_k_ff_2 (
    .J(and_4_out), .clk(in_1), .K(and_5_out), .Q(out_4[2]), .preset(and_6_out), .reset(and_11_out));  // open: Qn, en
  and and_11 (and_11_out, not_4_out, in_2);
  J_K_Flip_Flop j_k_ff_3 (
    .J(and_7_out), .clk(in_1), .K(and_8_out), .Q(out_4[4]), .preset(and_9_out), .reset(and_12_out));  // open: Qn, en
  and and_12 (and_12_out, not_6_out, in_2);
  and and_13 (and_13_out, 1'b1, out_4[0]);
  not not_7 (not_7_out, out_4[1]);
  and and_14 (and_14_out, and_13_out, not_7_out);
  and and_15 (and_15_out, out_4[1], and_13_out);
  and and_16 (and_16_out, pulso2, out_4[2]);
  not not_8 (not_8_out, out_4[3]);
  and and_17 (and_17_out, and_16_out, not_8_out);
  and and_18 (and_18_out, pulso4, out_4[4]);
  not not_9 (not_9_out, out_4[5]);
  and and_19 (and_19_out, and_18_out, not_9_out);
  J_K_Flip_Flop j_k_ff_4 (
    .J(and_14_out), .clk(in_1), .K(and_15_out), .Q(out_4[1]), .preset(and_20_out), .reset(and_21_out));  // open: Qn, en
  and and_20 (and_20_out, in_3[1], in_2);
  not not_10 (not_10_out, in_3[1]);
  and and_21 (and_21_out, not_10_out, in_2);
  and and_22 (and_22_out, out_4[3], and_16_out);
  J_K_Flip_Flop j_k_ff_5 (
    .J(and_17_out), .clk(in_1), .K(and_22_out), .Q(out_4[3]), .preset(and_23_out), .reset(and_24_out));  // open: Qn, en
  and and_23 (and_23_out, in_3[3], in_2);
  not not_11 (not_11_out, in_3[3]);
  and and_24 (and_24_out, not_11_out, in_2);
  and and_25 (and_25_out, out_4[5], and_18_out);
  J_K_Flip_Flop j_k_ff_6 (
    .J(and_19_out), .clk(in_1), .K(and_25_out), .Q(out_4[5]), .preset(and_26_out), .reset(and_27_out));  // open: Qn, en
  and and_26 (and_26_out, in_3[5], in_2);
  not not_12 (not_12_out, in_3[5]);
  and and_27 (and_27_out, not_12_out, in_2);
  and and_28 (pulso2, and_13_out, out_4[1]);
  and and_29 (pulso4, and_16_out, out_4[3]);
  and and_30 (pulso6, and_18_out, out_4[5]);
  not not_13 (not_13_out, out_4[6]);
  and and_31 (and_31_out, pulso6, not_13_out);
  and and_32 (and_32_out, out_4[6], pulso6);
  J_K_Flip_Flop j_k_ff_7 (
    .J(and_31_out), .clk(in_1), .K(and_32_out), .Q(out_4[6]), .preset(and_33_out), .reset(and_34_out));  // open: Qn, en
  and and_33 (and_33_out, in_3[6], in_2);
  not not_14 (not_14_out, in_3[6]);
  and and_34 (and_34_out, not_14_out, in_2);
  and and_35 (and_35_out, pulso6, out_4[6]);
  not not_15 (not_15_out, out_4[7]);
  and and_36 (and_36_out, and_35_out, not_15_out);
  and and_37 (and_37_out, out_4[7], and_35_out);
  J_K_Flip_Flop j_k_ff_8 (
    .J(and_36_out), .clk(in_1), .K(and_37_out), .Q(out_4[7]), .preset(and_38_out), .reset(and_39_out));  // open: Qn, en
  and and_38 (and_38_out, in_3[7], in_2);
  not not_16 (not_16_out, in_3[7]);
  and and_39 (and_39_out, not_16_out, in_2);
  and and_40 (pulso8, and_35_out, out_4[7]);

  // Other names for the same wires on the sheet: c = in_1; e1 = in_3[0]; e2 = in_3[1]; e3 = in_3[2]; e4 = in_3[3];
  //   e5 = in_3[4]; e6 = in_3[5]; e7 = in_3[6]; e8 = in_3[7]; s1 = out_4[0]; s2 = out_4[1]; s3 = out_4[2];
  //   s4 = out_4[3]; s5 = out_4[4]; s6 = out_4[5]; s7 = out_4[6]; s8 = out_4[7]; Setter = in_2
endmodule

module Controlador (
  input  in_1,
  input  [15:0] \Conteúdo_do_IR ,
  input  [15:0] in_3,
  output Memory_out_in,
  output IR_out_in,
  output PC_plus_plus,
  output out_7,
  output out_8,
  output out_9,
  output out_10,
  output out_11,
  output out_12,
  output [2:0] operacao,
  output ALU_fase_2,
  output ALU_fase_1,
  output DESVIO
);

  wire ADD, and_2_out, and_3_out, and_8_out, and_9_out, and_10_out, and_14_out, and_15_out, and_16_out,
       and_17_out, and_18_out, and_19_out, AUX0, AUX1, AUX2, AUX3, AUX4, AUX5, DIV, DZ, EQ, est0, est1, est2,
       GE, GT, JDZ, JEQ, JGE, JGT, JLE, JLT, JMP, JUMP_CONDICIONAL, LE, LT, MUL, nand_1_out, NOP_out,
       not_1_out, not_2_out, not_3_out, not_4_out, not_5_out, not_7_out, not_8_out, not_9_out, not_10_out,
       not_11_out, not_12_out, not_13_out, not_14_out, not_15_out, not_16_out, not_17_out, not_18_out,
       not_19_out, not_20_out, not_21_out, not_22_out, not_23_out, not_24_out, not_25_out, not_26_out,
       not_27_out, not_28_out, not_29_out, not_30_out, not_31_out, not_32_out, not_33_out, not_34_out, OP,
       or_1_out, or_2_out, or_7_out, or_9_out, REM, s1, s2, SUB;

  not not_1 (not_1_out, s1);
  not not_2 (not_2_out, s2);
  and and_1 (est0, not_2_out, not_1_out);
  not not_3 (not_3_out, s1);
  and and_2 (and_2_out, 1'b1, not_3_out);
  and and_3 (and_3_out, 1'b1, s1);
  J_K_Flip_Flop j_k_ff_1 (.J(and_2_out), .clk(in_1), .K(and_3_out), .Q(s1));  // open: Qn, preset, en, reset
  and and_4 (est1, s1, not_2_out);
  nor nor_1 (EQ, in_3[0], in_3[1], in_3[2], in_3[3], in_3[4], in_3[5], in_3[6], in_3[7], in_3[8], in_3[9], in_3[10], in_3[11], in_3[12], in_3[13], in_3[14], in_3[15]);
  or or_1 (or_1_out, in_3[0], in_3[1], in_3[2], in_3[3], in_3[4], in_3[5], in_3[6], in_3[7], in_3[8], in_3[9], in_3[10], in_3[11], in_3[12], in_3[13], in_3[14]);
  not not_4 (not_4_out, in_3[15]);
  or or_2 (or_2_out, in_3[0], in_3[1], in_3[2], in_3[3], in_3[4], in_3[5], in_3[6], in_3[7], in_3[8], in_3[9], in_3[10], in_3[11], in_3[12], in_3[13], in_3[14]);
  and and_5 (LT, or_2_out, in_3[15]);
  and and_6 (est2, s2, not_1_out);
  assign operacao = REM ? 3'b100 : 3'bz;  // Controlled_Buffer controlled_buffer_1
  and and_7 (GT, or_1_out, not_4_out);
  and and_8 (and_8_out, 1'b1, s1);
  not not_5 (not_5_out, s2);
  and and_9 (and_9_out, and_8_out, not_5_out);
  and and_10 (and_10_out, s2, and_8_out);
  Comparator comparator_1 (.a(\Conteúdo_do_IR [15:8]), .b(8'h19), .eq(REM));  // open: gt, lt
  Comparator comparator_2 (.a(\Conteúdo_do_IR [15:8]), .b(8'h18), .eq(DIV));  // open: gt, lt
  assign operacao = DIV ? 3'b011 : 3'bz;  // Controlled_Buffer controlled_buffer_2
  or or_3 (OP, REM, DIV, SUB, ADD, MUL);
  J_K_Flip_Flop j_k_ff_2 (.J(and_9_out), .clk(in_1), .K(and_10_out), .Q(s2));  // open: Qn, preset, en, reset
  and and_11 (out_7, s2, s1);
  assign operacao = MUL ? 3'b010 : 3'bz;  // Controlled_Buffer controlled_buffer_3
  not not_6 (DZ, EQ);
  or or_4 (GE, GT, EQ);
  or or_5 (LE, EQ, LT);
  and and_12 (ALU_fase_1, OP, not_7_out);
  not not_7 (not_7_out, ALU_fase_2);
  Register #(.width(6)) register_1 (
    .D({LE, DZ, GT, EQ, LT, GE}), .Q({AUX5, AUX4, AUX3, AUX2, AUX1, AUX0}), .clk(in_1));  // open: en, clr
  not not_8 (not_8_out, \Conteúdo_do_IR [10]);
  not not_9 (not_9_out, \Conteúdo_do_IR [12]);
  not not_10 (not_10_out, \Conteúdo_do_IR [13]);
  not not_11 (not_11_out, \Conteúdo_do_IR [14]);
  not not_12 (not_12_out, \Conteúdo_do_IR [15]);
  not not_13 (not_13_out, \Conteúdo_do_IR [8]);
  not not_14 (not_14_out, \Conteúdo_do_IR [9]);
  not not_15 (not_15_out, \Conteúdo_do_IR [12]);
  not not_16 (not_16_out, \Conteúdo_do_IR [13]);
  not not_17 (not_17_out, \Conteúdo_do_IR [14]);
  not not_18 (not_18_out, \Conteúdo_do_IR [15]);
  Comparator comparator_3 (.a(\Conteúdo_do_IR [15:8]), .b(8'h15), .eq(ADD));  // open: gt, lt
  assign operacao = SUB ? 3'b001 : 3'bz;  // Controlled_Buffer controlled_buffer_4
  // AND_Gate and_13 has open pins: in0=OP, in1=est2, out=open
  and LDA (out_8, \Conteúdo_do_IR [8], \Conteúdo_do_IR [9], not_8_out, \Conteúdo_do_IR [11], not_9_out, not_10_out, not_11_out, not_12_out);
  and STA (out_11, not_13_out, not_14_out, \Conteúdo_do_IR [10], \Conteúdo_do_IR [11], not_15_out, not_16_out, not_17_out, not_18_out);
  assign operacao = ADD ? 3'b000 : 3'bz;  // Controlled_Buffer controlled_buffer_5
  not not_19 (not_19_out, OP);
  assign operacao = not_19_out ? 3'b111 : 3'bz;  // Controlled_Buffer controlled_buffer_6
  D_Flip_Flop d_ff_1 (.clk(in_1), .D(ALU_fase_1), .Q(ALU_fase_2));  // open: Qn, preset, en, reset
  not not_20 (not_20_out, est1);
  nand nand_1 (nand_1_out, est1, est0);
  or or_6 (IR_out_in, est0, not_20_out);
  not not_21 (not_21_out, \Conteúdo_do_IR [10]);
  not not_22 (not_22_out, \Conteúdo_do_IR [11]);
  not not_23 (not_23_out, \Conteúdo_do_IR [14]);
  not not_24 (not_24_out, \Conteúdo_do_IR [15]);
  not not_25 (not_25_out, \Conteúdo_do_IR [8]);
  not not_26 (not_26_out, \Conteúdo_do_IR [11]);
  not not_27 (not_27_out, \Conteúdo_do_IR [12]);
  not not_28 (not_28_out, \Conteúdo_do_IR [13]);
  not not_29 (not_29_out, \Conteúdo_do_IR [15]);
  Comparator comparator_4 (.a(\Conteúdo_do_IR [15:8]), .b(8'h16), .eq(SUB));  // open: gt, lt
  Comparator comparator_5 (.a(\Conteúdo_do_IR [15:8]), .b(8'h34), .eq(JLE));  // open: gt, lt
  Comparator comparator_6 (.a(\Conteúdo_do_IR [15:8]), .b(8'h35), .eq(JDZ));  // open: gt, lt
  Comparator comparator_7 (.a(\Conteúdo_do_IR [15:8]), .b(8'h36), .eq(JGT));  // open: gt, lt
  Comparator comparator_8 (.a(\Conteúdo_do_IR [15:8]), .b(8'h37), .eq(JEQ));  // open: gt, lt
  Comparator comparator_9 (.a(\Conteúdo_do_IR [15:8]), .b(8'h38), .eq(JLT));  // open: gt, lt
  Comparator comparator_10 (.a(\Conteúdo_do_IR [15:8]), .b(8'h39), .eq(JGE));  // open: gt, lt
  or or_7 (or_7_out, out_11, out_9);
  and NOP (NOP_out, \Conteúdo_do_IR [8], \Conteúdo_do_IR [9], not_21_out, not_22_out, \Conteúdo_do_IR [12], \Conteúdo_do_IR [13], not_23_out, not_24_out);
  and STP (out_10, not_25_out, \Conteúdo_do_IR [9], \Conteúdo_do_IR [10], not_26_out, not_27_out, not_28_out, \Conteúdo_do_IR [14], not_29_out);
  xor xor_1 (Memory_out_in, nand_1_out, or_7_out);
  and and_14 (and_14_out, AUX0, JGE);
  and and_15 (and_15_out, AUX1, JLT);
  and and_16 (and_16_out, AUX2, JEQ);
  and and_17 (and_17_out, AUX3, JGT);
  and and_18 (and_18_out, AUX4, JDZ);
  and and_19 (and_19_out, AUX5, JLE);
  not not_30 (not_30_out, \Conteúdo_do_IR [10]);
  not not_31 (not_31_out, \Conteúdo_do_IR [11]);
  not not_32 (not_32_out, \Conteúdo_do_IR [14]);
  not not_33 (not_33_out, \Conteúdo_do_IR [15]);
  Comparator comparator_11 (.a(\Conteúdo_do_IR [15:8]), .b(8'h17), .eq(MUL));  // open: gt, lt
  or or_8 (JUMP_CONDICIONAL, and_14_out, and_15_out, and_16_out, and_17_out, and_18_out, and_19_out);
  or or_9 (or_9_out, JMP, JUMP_CONDICIONAL);
  and u_JMP (JMP, \Conteúdo_do_IR [8], \Conteúdo_do_IR [9], not_30_out, not_31_out, \Conteúdo_do_IR [12], \Conteúdo_do_IR [13], not_32_out, not_33_out);
  Comparator comparator_12 (.a(\Conteúdo_do_IR [15:8]), .b(8'h1f), .eq(out_9));  // open: gt, lt
  Comparator comparator_13 (.a(\Conteúdo_do_IR [15:8]), .b(8'h29), .eq(out_12));  // open: gt, lt
  not not_34 (not_34_out, out_7);
  and and_20 (DESVIO, not_34_out, or_9_out);

  assign PC_plus_plus = out_7;

  // Other names for the same wires on the sheet: ACC_in[15:0] = in_3; ALUfase2 = ALU_fase_2; c = in_1; est3 = out_7;
  //   INN = out_9; IR_In[15:0] = \Conteúdo_do_IR ; PRN = out_12; STA = out_11

  // Notes on the sheet:
  //   Estado 0
  //   valor contido no ACC. Usado para pulos condicionais.
  //   Estado 1
  //   Estado 2
  //   OP.ARITM
  //   Estado 3
endmodule

module Main (
  input  [15:0] in_1
);

  wire alu_1_div0, alu_1_overflow, and_1_out, and_2_out, Clock, clock_1_out, controlador_1_desvio,
       controlador_1_ir_out_in, controlador_1_memory_out_in, controlador_1_pc_plus_plus, INN, IRCLEAR, LDA,
       not_1_out, not_2_out, not_3_out, not_4_out, not_5_out, not_6_out, not_7_out, or_1_out, PRN, Set, STA,
       STOP, Unset;
  wire [2:0] SETTER;
  wire [3:0] controlled_buffer_2_out_2, controlled_buffer_2_out_3;
  wire [7:0] controlled_buffer_2_out, controlled_buffer_4_out, Endereco, multiplexer_2_out, pc_1_out_4;
  wire [15:0] alu_1_out_8, controlled_buffer_1_out, controlled_buffer_3_out, controlled_buffer_6_out,
       demultiplexer_1_out0, demultiplexer_1_out1, multiplexer_1_out, ValorACC;
  wire [15:8] IR_q;

  Hex_Digit_Display hex_digit_display_1 (.value(controlled_buffer_2_out_3));  // open: dp
  Hex_Digit_Display hex_digit_display_2 (.value(controlled_buffer_2_out_2));  // open: dp
  Hex_Digit_Display hex_digit_display_3 (.value(controlled_buffer_2_out[7:4]));  // open: dp
  Hex_Digit_Display hex_digit_display_4 (.value(controlled_buffer_2_out[3:0]));  // open: dp
  assign controlled_buffer_1_out = INN ? in_1 : 16'bz;  // Controlled_Buffer controlled_buffer_1
  assign {controlled_buffer_2_out_3, controlled_buffer_2_out_2, controlled_buffer_2_out} = PRN ? controlled_buffer_1_out : 16'bz;  // Controlled_Buffer controlled_buffer_2
  RAM #(.dataWidth(16)) ram_1 (
    .addr(multiplexer_2_out), .data(controlled_buffer_1_out), .clk(Clock), .ld(controlador_1_memory_out_in));  // open: sel, clr
  assign controlled_buffer_3_out = LDA ? controlled_buffer_1_out : 16'bz;  // Controlled_Buffer controlled_buffer_3
  Controlador controlador_1 (
    .Memory_out_in(controlador_1_memory_out_in), .IR_out_in(controlador_1_ir_out_in),
    .\Conteúdo_do_IR ({IR_q, Endereco}), .PC_plus_plus(controlador_1_pc_plus_plus), .in_1(Clock),
    .out_8(LDA), .out_10(STOP), .out_11(STA), .ALU_fase_1(Set), .operacao(SETTER), .ALU_fase_2(Unset),
    .in_3(ValorACC), .DESVIO(controlador_1_desvio), .out_7(IRCLEAR), .out_9(INN), .out_12(PRN));
  Multiplexer #(.width(16), .enable("false")) multiplexer_1 (
    .in0(alu_1_out_8), .in1(controlled_buffer_3_out), .out(multiplexer_1_out), .sel(not_1_out));
  Register #(.width(16)) ACC (.D(multiplexer_1_out), .Q(ValorACC), .clk(Clock));  // open: en, clr
  not not_1 (not_1_out, Unset);
  assign controlled_buffer_4_out = controlador_1_desvio ? Endereco : 8'bz;  // Controlled_Buffer controlled_buffer_4
  Demultiplexer #(.width(16), .enable("false")) demultiplexer_1 (
    .out0(demultiplexer_1_out0), .out1(demultiplexer_1_out1), .in(ValorACC), .sel(not_2_out));
  not not_2 (not_2_out, Set);
  assign controlled_buffer_1_out = STA ? demultiplexer_1_out1 : 16'bz;  // Controlled_Buffer controlled_buffer_5
  Multiplexer #(.width(8), .enable("false")) multiplexer_2 (
    .in0(pc_1_out_4), .in1(Endereco), .out(multiplexer_2_out), .sel(or_1_out));
  or or_1 (or_1_out, LDA, Set, STA, INN, PRN);
  PC pc_1 (
    .out_4(pc_1_out_4), .in_1(controlador_1_pc_plus_plus), .in_3(controlled_buffer_4_out),
    .in_2(controlador_1_desvio));
  ALU alu_1 (
    .s(SETTER), .Div0(alu_1_div0), .Set_mode(Set), .Overflow(alu_1_overflow), .out_8(alu_1_out_8),
    .in_2(controlled_buffer_1_out), .in_1(demultiplexer_1_out0));  // open: Clear
  assign controlled_buffer_6_out = and_1_out ? controlled_buffer_1_out : 16'bz;  // Controlled_Buffer controlled_buffer_6
  and and_1 (and_1_out, not_4_out, not_3_out);
  not not_3 (not_3_out, INN);
  not not_4 (not_4_out, STA);
  Register #(.width(16)) IR (
    .D(controlled_buffer_6_out), .Q({IR_q, Endereco}), .clk(controlador_1_ir_out_in), .clr(IRCLEAR));  // open: en
  not not_5 (not_5_out, alu_1_div0);
  not not_6 (not_6_out, alu_1_overflow);
  not not_7 (not_7_out, STOP);
  Clock clock_1 (.out(clock_1_out));
  and and_2 (and_2_out, not_5_out, not_6_out, not_7_out);
  and and_3 (Clock, clock_1_out, and_2_out);

  // Notes on the sheet:
  //   SAÍDA
  //   ENTRADA
endmodule
